// Logisim project ampm.circ as structural Verilog: 1 circuit, main circuit main
module main (
  input  in_1,
  output out_2,
  output out_3
);

  wire and_1_out;
  wire [3:0] counter_1_q;

  Counter #(.width(4), .max('hb)) counter_1 (.Q(counter_1_q), .clk(in_1));  // open: load, D, count, carry, clr
  and and_1 (and_1_out, counter_1_q[0], counter_1_q[1], counter_1_q[3]);
  T_Flip_Flop t_ff_1 (.clk(in_1), .T(and_1_out), .Q(out_2), .Qn(out_3));  // open: preset, reset, en
endmodule
