// Logisim project mod 12.circ as structural Verilog: 2 circuits, main circuit main
module main (
  input  clock,
  input  enable,
  output q0,
  output q1,
  output q2,
  output q3
);

  wire and_1_out, j_k_ff_1_qn, j_k_ff_2_qn, j_k_ff_3_qn;

  J_K_Flip_Flop j_k_ff_1 (
    .J(1'b1), .clk(clock), .K(1'b1), .Q(q0), .Qn(j_k_ff_1_qn), .preset(and_1_out), .en(enable));  // open: reset
  J_K_Flip_Flop j_k_ff_2 (
    .J(1'b1), .clk(j_k_ff_1_qn), .K(1'b1), .Q(q1), .Qn(j_k_ff_2_qn), .en(enable), .reset(and_1_out));  // open: preset
  J_K_Flip_Flop j_k_ff_3 (
    .J(1'b1), .clk(j_k_ff_2_qn), .K(1'b1), .Q(q2), .Qn(j_k_ff_3_qn), .en(enable), .reset(and_1_out));  // open: preset
  and and_1 (and_1_out, q0, j_k_ff_2_qn, q2, q3);
  J_K_Flip_Flop j_k_ff_4 (
    .J(1'b1), .clk(j_k_ff_3_qn), .K(1'b1), .Q(q3), .en(enable), .reset(and_1_out));  // open: Qn, preset
endmodule

module f (
  input  enable,
  input  clock,
  output q3,
  output q2,
  output q1,
  output q0,
  output select
);

  wire and_1_out, and_2_out, and_3_out, main_1_q0, main_1_q1, main_1_q2, main_1_q3, or_1_out;

  Multiplexer #(.disabled(0), .enable("false")) multiplexer_1 (.in0(1'b0), .in1(main_1_q3), .out(q3), .sel(select));
  main main_1 (.clock(clock), .enable(enable), .q0(main_1_q0), .q1(main_1_q1), .q2(main_1_q2), .q3(main_1_q3));
  and and_1 (and_1_out, main_1_q3, main_1_q2);
  Multiplexer #(.disabled(0), .enable("false")) multiplexer_2 (.in0(1'b0), .in1(main_1_q2), .out(q2), .sel(select));
  Multiplexer #(.disabled(0), .enable("false")) multiplexer_3 (
    .in0(and_1_out), .in1(main_1_q1), .out(q1), .sel(select));
  and and_2 (and_2_out, main_1_q1, main_1_q0);
  Multiplexer #(.disabled(0), .enable("false")) multiplexer_4 (
    .in0(and_2_out), .in1(main_1_q0), .out(q0), .sel(select));
  or or_1 (or_1_out, main_1_q1, main_1_q2);
  and and_3 (and_3_out, or_1_out, main_1_q3);
  not not_1 (select, and_3_out);
endmodule
