// Logisim project new mod 6.circ as structural Verilog: 1 circuit, main circuit main
module main (
  input  clock,
  input  enable,
  output q1,
  output q2,
  output q3,
  output q4,
  output rc
);

  wire and_1_out, and_2_out, and_3_out;

  J_K_Flip_Flop j_k_ff_1 (.J(1'b1), .clk(clock), .K(1'b1), .Q(q1), .en(enable), .reset(and_1_out));  // open: Qn, preset
  J_K_Flip_Flop j_k_ff_2 (.J(q1), .clk(clock), .K(q1), .Q(q2), .en(enable), .reset(and_1_out));  // open: Qn, preset
  and and_1 (and_1_out, q2, q3);
  and and_2 (and_2_out, q1, q2);
  J_K_Flip_Flop j_k_ff_3 (
    .J(and_2_out), .clk(clock), .K(and_2_out), .Q(q3), .en(enable), .reset(and_1_out));  // open: Qn, preset
  J_K_Flip_Flop j_k_ff_4 (.Q(q4));  // open: J, clk, K, Qn, preset, en, reset
  and and_3 (and_3_out, q3, q1);
  D_Flip_Flop d_ff_1 (.clk(clock), .D(and_3_out), .Q(rc));  // open: Qn, preset, en, reset
endmodule
