// Logisim project new.circ as structural Verilog: 2 circuits, main circuit main
// BCD to 7SEGMENT
module main (
  input  q0,
  input  in_2,
  input  q2,
  input  q3,
  output f,
  output e,
  output g,
  output d,
  output c,
  output b,
  output a
);

  wire and_1_out, and_2_out, and_3_out, and_4_out, and_5_out, not_1_out, not_2_out, not_3_out, not_4_out,
       not_5_out, not_6_out, not_7_out, not_8_out, not_9_out, not_10_out, not_11_out, not_12_out, not_13_out,
       not_14_out, not_15_out, not_16_out, not_17_out, not_18_out, not_19_out, or_1_out, or_2_out, or_4_out,
       or_5_out, or_6_out, or_7_out, or_9_out, or_10_out, or_12_out, or_13_out, or_15_out, or_16_out,
       or_18_out, or_19_out, or_20_out, or_21_out, or_23_out, or_24_out;

  not not_1 (not_1_out, or_1_out);
  not not_2 (not_2_out, or_4_out);
  not not_3 (not_3_out, or_5_out);
  not not_4 (not_4_out, or_7_out);
  not not_5 (not_5_out, or_9_out);
  not not_6 (not_6_out, or_12_out);
  not not_7 (not_7_out, or_15_out);
  or or_1 (or_1_out, q3, q2, in_2, q0);
  or or_2 (or_2_out, in_2, q2);
  or or_3 (f, not_7_out, not_6_out, not_5_out, not_3_out, not_2_out, not_1_out);
  not not_8 (not_8_out, or_18_out);
  not not_9 (not_9_out, or_20_out);
  not not_10 (not_10_out, or_23_out);
  or or_4 (or_4_out, or_2_out, not_11_out);
  or or_5 (or_5_out, or_6_out, not_12_out);
  not not_11 (not_11_out, and_1_out);
  or or_6 (or_6_out, q0, in_2, q2);
  and and_1 (and_1_out, q3, q0);
  or or_7 (or_7_out, not_13_out, q3);
  not not_12 (not_12_out, q3);
  not not_13 (not_13_out, and_2_out);
  and and_2 (and_2_out, q0, in_2, q2);
  or or_8 (g, not_9_out, not_8_out, not_7_out, not_6_out, not_5_out, not_3_out, not_2_out);
  or or_9 (or_9_out, not_14_out, or_10_out);
  not not_14 (not_14_out, and_3_out);
  or or_10 (or_10_out, q0, q3);
  and and_3 (and_3_out, in_2, q2);
  or or_11 (e, not_9_out, not_5_out, not_3_out, not_1_out);
  or or_12 (or_12_out, not_15_out, or_13_out);
  not not_15 (not_15_out, and_4_out);
  and and_4 (and_4_out, q0, q2);
  or or_13 (or_13_out, in_2, q3);
  or or_14 (d, not_9_out, not_8_out, not_6_out, not_5_out, not_3_out, not_2_out, not_1_out);
  or or_15 (or_15_out, or_16_out, not_16_out);
  not not_16 (not_16_out, q2);
  or or_16 (or_16_out, q0, in_2, q3);
  or or_17 (c, not_10_out, not_8_out, not_7_out, not_6_out, not_5_out, not_4_out, not_3_out, not_2_out, not_1_out);
  or or_18 (or_18_out, or_19_out, not_17_out);
  not not_17 (not_17_out, and_5_out);
  or or_19 (or_19_out, q3, q2);
  and and_5 (and_5_out, in_2, q0);
  or or_20 (or_20_out, or_21_out, not_18_out);
  not not_18 (not_18_out, in_2);
  or or_21 (or_21_out, q3, q2, q0);
  or or_22 (b, not_10_out, not_9_out, not_8_out, not_7_out, not_4_out, not_3_out, not_2_out, not_1_out);
  or or_23 (or_23_out, or_24_out, not_19_out);
  not not_19 (not_19_out, q0);
  or or_24 (or_24_out, q3, q2, in_2);
  or or_25 (a, not_1_out, not_2_out, not_3_out, not_4_out, not_5_out, not_6_out, not_8_out, not_9_out);
endmodule

module \final  (
);

  wire clock_1_out, f_1_q0, f_1_q1, f_1_q2, f_1_q3, f_1_select, main_1_a, main_1_b, main_1_c, main_1_d,
       main_1_e, main_1_f, main_1_g, main_2_a, main_2_b, main_2_c, main_2_d, main_2_e, main_2_f, main_2_g,
       main_3_q1, main_3_q2, main_3_q3, main_3_q4, main_3_rc, main_4_a, main_4_b, main_4_c, main_4_d,
       main_4_e, main_4_f, main_4_g, main_5_q1, main_5_q2, main_5_q3, main_5_q4, main_5_rc, main_6_a,
       main_6_b, main_6_c, main_6_d, main_6_e, main_6_f, main_6_g, main_7_q1, main_7_q2, main_7_q3,
       main_7_q4, main_7_rc, main_8_a, main_8_b, main_8_c, main_8_d, main_8_e, main_8_f, main_8_g, main_9_q1,
       main_9_q2, main_9_q3, main_9_q4, main_9_rc, main_10_a, main_10_b, main_10_c, main_10_d, main_10_e,
       main_10_f, main_10_g, main_11_out_2, main_11_out_3, not_1_out;

  _7_Segment_Display u_7_segment_display_1 (
    .g(main_1_g), .f(main_1_f), .a(main_1_a), .b(main_1_b), .e(main_1_e), .d(main_1_d), .c(main_1_c));  // open: dp
  not not_1 (not_1_out, f_1_select);
  main main_1 (
    .f(main_1_f), .g(main_1_g), .e(main_1_e), .d(main_1_d), .c(main_1_c), .b(main_1_b), .a(main_1_a),
    .q0(not_1_out), .in_2(1'b0), .q2(1'b0), .q3(1'b0));
  _7_Segment_Display u_7_segment_display_2 (
    .g(main_2_g), .f(main_2_f), .a(main_2_a), .b(main_2_b), .e(main_2_e), .d(main_2_d), .c(main_2_c));  // open: dp
  f f_1 (.q3(f_1_q3), .q2(f_1_q2), .q1(f_1_q1), .q0(f_1_q0), .select(f_1_select), .clock(main_3_rc));  // open: enable
  main main_2 (
    .f(main_2_f), .g(main_2_g), .e(main_2_e), .d(main_2_d), .c(main_2_c), .b(main_2_b), .a(main_2_a),
    .q0(f_1_q0), .in_2(f_1_q1), .q2(f_1_q2), .q3(f_1_q3));
  new_mod_6_main main_3 (
    .clock(main_5_rc), .q1(main_3_q1), .q2(main_3_q2), .q3(main_3_q3), .q4(main_3_q4), .rc(main_3_rc));  // open: enable
  _7_Segment_Display u_7_segment_display_3 (
    .g(main_4_g), .f(main_4_f), .a(main_4_a), .b(main_4_b), .e(main_4_e), .d(main_4_d), .c(main_4_c));  // open: dp
  main main_4 (
    .f(main_4_f), .g(main_4_g), .e(main_4_e), .d(main_4_d), .c(main_4_c), .b(main_4_b), .a(main_4_a),
    .q0(main_3_q1), .in_2(main_3_q2), .q2(main_3_q3), .q3(main_3_q4));
  _7_Segment_Display u_7_segment_display_4 (
    .g(main_6_g), .f(main_6_f), .a(main_6_a), .b(main_6_b), .e(main_6_e), .d(main_6_d), .c(main_6_c));  // open: dp
  new_mod_10_main main_5 (
    .in_1(main_7_rc), .q1(main_5_q1), .q2(main_5_q2), .q3(main_5_q3), .q4(main_5_q4), .rc(main_5_rc));  // open: enable
  main main_6 (
    .f(main_6_f), .g(main_6_g), .e(main_6_e), .d(main_6_d), .c(main_6_c), .b(main_6_b), .a(main_6_a),
    .q0(main_5_q1), .in_2(main_5_q2), .q2(main_5_q3), .q3(main_5_q4));
  new_mod_6_main main_7 (
    .clock(main_9_rc), .q1(main_7_q1), .q2(main_7_q2), .q3(main_7_q3), .q4(main_7_q4), .rc(main_7_rc));  // open: enable
  _7_Segment_Display u_7_segment_display_5 (
    .g(main_8_g), .f(main_8_f), .a(main_8_a), .b(main_8_b), .e(main_8_e), .d(main_8_d), .c(main_8_c));  // open: dp
  main main_8 (
    .f(main_8_f), .g(main_8_g), .e(main_8_e), .d(main_8_d), .c(main_8_c), .b(main_8_b), .a(main_8_a),
    .q0(main_7_q1), .in_2(main_7_q2), .q2(main_7_q3), .q3(main_7_q4));
  _7_Segment_Display u_7_segment_display_6 (
    .g(main_10_g), .f(main_10_f), .a(main_10_a), .b(main_10_b), .e(main_10_e), .d(main_10_d), .c(main_10_c));  // open: dp
  new_mod_10_main main_9 (
    .in_1(clock_1_out), .q1(main_9_q1), .q2(main_9_q2), .q3(main_9_q3), .q4(main_9_q4), .enable(1'b1),
    .rc(main_9_rc));
  main main_10 (
    .f(main_10_f), .g(main_10_g), .e(main_10_e), .d(main_10_d), .c(main_10_c), .b(main_10_b), .a(main_10_a),
    .q0(main_9_q1), .in_2(main_9_q2), .q2(main_9_q3), .q3(main_9_q4));
  Clock clock_1 (.out(clock_1_out));
  LED led_1 (.in(main_11_out_2));
  LED led_2 (.in(main_11_out_3));
  ampm_main main_11 (.in_1(main_3_rc), .out_2(main_11_out_2), .out_3(main_11_out_3));

  // Notes on the sheet:
  //   HOURS
  //   MOD-12
  //   MOD-6
  //   DIGITAL CLOCK
  //   MINUTES
  //   MOD-10
  //   MOD-6
  //   SECONDS
  //   MOD-10
  //   PM
  //   AM
  //   MOD-12
endmodule
